// Digital circuit VendingMachine.dig as structural Verilog
module VendingMachine (
  input  di,
  input  ni,
  input  qi,
  input  C
);

  wire and_1_out, and_2_out, and_3_out, and_9_out, and_10_out, and_11_out, and_12_out, and_13_out,
       and_14_out, and_15_out, and_16_out, and_17_out, and_18_out, and_19_out, and_20_out, and_21_out,
       and_22_out, and_23_out, and_24_out, and_25_out, and_26_out, and_27_out, and_28_out, and_29_out,
       and_30_out, and_31_out, and_32_out, and_33_out, and_34_out, and_35_out, and_36_out, and_40_out,
       and_41_out, btn, btnEdge, clk, clkPrev, co, D_1, D_2, D_3, D_4, D_5, d_ff_as_2_nq, d_ff_as_3_nq, di_t,
       \do , ni_t, no, not_1_out, not_2_out, not_3_out, not_4_out, not_5_out, not_6_out, not_7_out,
       not_8_out, or_2_out, or_6_out, or_7_out, or_8_out, qi_t, rst, slow, trigger, Z_1_n, Z_2_n;
  wire [2:1] or_11_out;
  wire [3:0] not_9_out, not_10_out, not_11_out, not_12_out, not_13_out, not_13_out_2, not_14_out,
       not_14_out_2;
  wire [5:0] add_1_s, d_ff_as_1_q;
  wire [7:0] multiplexer_1_out, multiplexer_2_out, multiplexer_3_out, multiplexer_4_out, multiplexer_5_out;
  wire [7:4] not_9_out_2, not_10_out_2, not_11_out_2, not_12_out_2;

  D_FF_AS #(.Bits(6)) d_ff_as_1 (.Set(1'b0), .D(add_1_s), .C(C), .Clr(rst), .Q(d_ff_as_1_q));  // open: nQ
  D_FF_AS d_ff_as_2 (.Set(1'b0), .D(clkPrev), .C(C), .Clr(rst), .Q(clk), .nQ(d_ff_as_2_nq));
  not not_1 (not_1_out, slow);
  not not_2 (not_2_out, trigger);
  Add #(.Bits(6)) add_1 (.a(d_ff_as_1_q), .b({{5{1'b0}}, slow}), .c_i(1'b0), .s(add_1_s));  // open: c_o
  D_FF_AS d_ff_as_3 (.Set(1'b0), .D(btn), .C(clk), .Clr(rst), .nQ(d_ff_as_3_nq));  // open: Q
  and and_1 (and_1_out, d_ff_as_2_nq, not_1_out);
  and and_2 (and_2_out, clk, slow, not_2_out);
  and and_3 (and_3_out, d_ff_as_2_nq, trigger);
  and and_4 (btnEdge, btn, d_ff_as_3_nq);
  or or_1 (clkPrev, and_1_out, and_2_out, and_3_out);
  and and_5 (trigger, add_1_s[0], add_1_s[1], add_1_s[2], add_1_s[3], add_1_s[4], add_1_s[5]);
  and and_6 (qi_t, btnEdge, qi);
  not not_3 (not_3_out, qi_t);
  and and_7 (di_t, btnEdge, di);
  not not_4 (not_4_out, di_t);
  and and_8 (ni_t, btnEdge, ni);
  not not_5 (not_5_out, ni_t);
  not not_6 (not_6_out, Z_2_n);
  Button reset (.out(rst));
  Button insert (.out(btn));
  not not_7 (not_7_out, Z_1_n);
  not not_8 (not_8_out, D_5);
  and and_9 (and_9_out, D_5, Z_1_n, not_6_out, not_4_out, not_5_out, qi_t);
  and and_10 (and_10_out, not_8_out, not_7_out, Z_2_n, not_4_out, not_5_out, qi_t);
  and and_11 (and_11_out, not_8_out, not_6_out, not_4_out, not_5_out, qi_t);
  and and_12 (and_12_out, not_8_out, not_7_out, Z_2_n, not_3_out);
  and and_13 (and_13_out, D_5, Z_1_n, not_6_out, ni_t);
  and and_14 (and_14_out, not_8_out, not_7_out, Z_2_n, ni_t);
  and and_15 (and_15_out, not_8_out, not_7_out, Z_2_n, di_t);
  and and_16 (and_16_out, not_7_out, not_6_out, not_4_out, not_5_out, qi_t);
  and and_17 (and_17_out, Z_1_n, not_6_out, di_t, not_5_out);
  and and_18 (and_18_out, D_5, not_7_out, not_6_out, qi_t);
  and and_19 (and_19_out, not_8_out, not_7_out, di_t, not_5_out);
  and and_20 (and_20_out, D_5, not_7_out, not_6_out, ni_t);
  and and_21 (and_21_out, not_8_out, Z_1_n, not_6_out, ni_t);
  and and_22 (and_22_out, not_8_out, Z_1_n, not_6_out, not_4_out);
  and and_23 (and_23_out, Z_1_n, not_6_out, not_4_out, not_5_out, not_3_out);
  and and_24 (and_24_out, not_7_out, not_6_out, di_t, not_5_out);
  and and_25 (and_25_out, D_5, not_6_out, not_5_out, not_3_out);
  and and_26 (and_26_out, not_8_out, not_7_out, not_4_out, qi_t);
  and and_27 (and_27_out, not_8_out, not_6_out, not_4_out, qi_t);
  and and_28 (and_28_out, D_5, not_6_out, di_t, not_5_out);
  and and_29 (and_29_out, not_8_out, not_7_out, ni_t);
  and and_30 (and_30_out, not_8_out, not_6_out, ni_t);
  and and_31 (and_31_out, D_5, Z_2_n);
  and and_32 (and_32_out, Z_1_n, Z_2_n);
  and and_33 (and_33_out, not_8_out, Z_1_n, Z_2_n);
  and and_34 (and_34_out, not_8_out, D_4);
  and and_35 (and_35_out, D_5, Z_1_n, Z_2_n);
  and and_36 (and_36_out, D_5, D_4);
  and and_37 (D_1, Z_1_n, not_6_out);
  and and_38 (D_2, not_7_out, Z_2_n);
  and and_39 (D_3, Z_1_n, Z_2_n);
  and and_40 (and_40_out, D_5, Z_2_n);
  and and_41 (and_41_out, Z_1_n, Z_2_n);
  or or_2 (or_2_out, and_9_out, and_10_out);
  or or_3 (co, and_31_out, and_32_out);
  or or_4 (no, and_33_out, and_34_out);
  or or_5 (\do , and_35_out, and_36_out);
  or or_6 (or_6_out, and_11_out, and_12_out, and_13_out, and_14_out, and_15_out, and_16_out, and_17_out, D_4);
  or or_7 (or_7_out, and_18_out, and_19_out, and_20_out, and_21_out, and_22_out, and_23_out, and_24_out, D_4);
  or or_8 (or_8_out, and_25_out, and_26_out, and_27_out, and_28_out, and_29_out, and_30_out, D_4);
  or or_9 (slow, and_40_out, D_4, and_41_out);
  Multiplexer #(.Bits(8)) multiplexer_1 (.sel(co), .in_0(8'h40), .in_1(8'h79), .out(multiplexer_1_out));
  assign {not_9_out_2, not_9_out} = ~multiplexer_1_out;  // Not not_9, 8 bits wide
  Seven_Seg seven_seg_1 (
    .a(not_9_out[0]), .b(not_9_out[1]), .c(not_9_out[2]), .d(not_9_out[3]), .e(not_9_out_2[4]),
    .f(not_9_out_2[5]), .g(not_9_out_2[6]), .dp(not_9_out_2[7]));
  assign {not_10_out_2, not_10_out} = ~{8{1'b1}};  // Not not_10, 8 bits wide
  Seven_Seg seven_seg_2 (
    .a(not_10_out[0]), .b(not_10_out[1]), .c(not_10_out[2]), .d(not_10_out[3]), .e(not_10_out_2[4]),
    .f(not_10_out_2[5]), .g(not_10_out_2[6]), .dp(not_10_out_2[7]));
  D_FF_AS Z_3_n (.Set(1'b0), .D(or_2_out), .C(clk), .Clr(rst), .Q(D_4));  // open: nQ
  D_FF_AS u_Z_2_n (.Set(1'b0), .D(or_6_out), .C(clk), .Clr(rst), .Q(Z_2_n));  // open: nQ
  D_FF_AS u_Z_1_n (.Set(1'b0), .D(or_7_out), .C(clk), .Clr(rst), .Q(Z_1_n));  // open: nQ
  D_FF_AS Z_0_n (.Set(1'b0), .D(or_8_out), .C(clk), .Clr(rst), .Q(D_5));  // open: nQ
  Multiplexer #(.Bits(8)) multiplexer_2 (.sel(\do ), .in_0(8'h40), .in_1(8'h79), .out(multiplexer_2_out));
  assign {not_11_out_2, not_11_out} = ~multiplexer_2_out;  // Not not_11, 8 bits wide
  Seven_Seg seven_seg_3 (
    .a(not_11_out[0]), .b(not_11_out[1]), .c(not_11_out[2]), .d(not_11_out[3]), .e(not_11_out_2[4]),
    .f(not_11_out_2[5]), .g(not_11_out_2[6]), .dp(not_11_out_2[7]));
  or or_10 (or_11_out[1], D_2, D_4);
  or or_11 (or_11_out[2], D_3, D_4);
  Multiplexer #(.Bits(8)) multiplexer_3 (.sel(no), .in_0(8'h40), .in_1(8'h12), .out(multiplexer_3_out));
  assign {not_12_out_2, not_12_out} = ~multiplexer_3_out;  // Not not_12, 8 bits wide
  Seven_Seg seven_seg_4 (
    .a(not_12_out[0]), .b(not_12_out[1]), .c(not_12_out[2]), .d(not_12_out[3]), .e(not_12_out_2[4]),
    .f(not_12_out_2[5]), .g(not_12_out_2[6]), .dp(not_12_out_2[7]));
  Multiplexer #(.Bits(8), .Selector_Bits(3)) multiplexer_4 (
    .sel({or_11_out, D_1}), .in_0(8'h40), .in_1(8'h79), .in_2(8'h24), .in_3({8{1'b1}}), .in_4(8'h30),
    .in_5({8{1'b1}}), .in_6(8'h19), .in_7({8{1'b1}}), .out(multiplexer_4_out));
  Seven_Seg seven_seg_5 (
    .a(not_13_out[0]), .b(not_13_out[1]), .c(not_13_out[2]), .d(not_13_out[3]), .e(not_13_out_2[0]),
    .f(not_13_out_2[1]), .g(not_13_out_2[2]), .dp(not_13_out_2[3]));
  assign {not_13_out_2, not_13_out} = ~multiplexer_4_out;  // Not not_13, 8 bits wide
  // Probe VendingMachine.fsm on {qi_t, ni_t, di_t, D_4, Z_2_n, Z_1_n, D_5}
  Seven_Seg seven_seg_6 (
    .a(not_14_out[0]), .b(not_14_out[1]), .c(not_14_out[2]), .d(not_14_out[3]), .e(not_14_out_2[0]),
    .f(not_14_out_2[1]), .g(not_14_out_2[2]), .dp(not_14_out_2[3]));
  assign {not_14_out_2, not_14_out} = ~multiplexer_5_out;  // Not not_14, 8 bits wide
  Multiplexer #(.Bits(8)) multiplexer_5 (.sel(D_5), .in_0(8'h40), .in_1(8'h12), .out(multiplexer_5_out));

  // Other names for the same wires on the sheet: Z_0_n = D_5; Z_3_n = D_4

  // Notes on the sheet:
  //   C: Hz: 50
endmodule
